# Fritzing sketch tapsterbot_pcb (saved by Fritzing 0.8.5b)
circuit board: 6.88566cm x 5.36311cm
breadboards: 1

parts:
  S2 = Basic Servo
  S3 = Basic Servo
  Bauteil1 = Arduino Uno (Rev3)
  S1 = Basic Servo
  STYLUS = male pin header, 1 pin [form="♂ (male)"]

nets:
  GND: S2.gnd, S3.gnd, Bauteil1.GND, S1.gnd, STYLUS.pin1
  VCC: S2.vcc, S3.vcc, Bauteil1.5V, S1.vcc
  N1: S2.pulse, Bauteil1.D10_PWM/SS
  N2: S3.pulse, Bauteil1.D9_PWM
  N3: Bauteil1.D11_PWM/MOSI, S1.pulse

notes:
  Tapsterbot
