# Fritzing sketch tapsterbot_instructions (saved by Fritzing 0.8.5b)
breadboards: 1

parts:
  Bauteil1 = Arduino Prototyping Shield
  J1 = Basic Servo
  J2 = Basic Servo
  J3 = Basic Servo
  J4 = female pin header, 2 pins [form="♀ (female)"]

nets:
  VCC: Bauteil1.+5V, J1.vcc, J2.vcc, J3.vcc
  GND: Bauteil1.GND, J1.gnd, J2.gnd, J3.gnd, J4.pin2
  N1: Bauteil1.D9, J1.pulse
  N2: Bauteil1.D10, J3.pulse
  N3: Bauteil1.D11, J2.pulse

notes:
  Stylus
